# Fritzing sketch Raspberry-py led (saved by Fritzing 0.9.3b)
breadboards: 1

parts:
  Raspberry_Pi_1 = Raspberry Pi 3 [part_number=RPI-3-V1.2]
  R1 = Resistor [tolerance=±5% resistance=1 package="2010 [SMD]"]
  LED1 = LED - 3mm [color="Red (633nm)" package="3 mm [THT]"]

nets:
  N1: Raspberry_Pi_1.GND, R1.Pin_1
  N2: Raspberry_Pi_1.GPIO18, LED1.cathode
  N3: R1.Pin_0, LED1.anode
